# Fritzing sketch vezdeUltrasonicScheme (saved by Fritzing 0.9.5d)

parts:
  Part1 = Arduino Uno (Rev3)
  HC-SR04_Sensor_1 = HC-SR04 Ultrasonic Distance Sensor
  LCD1 = LCD screen  # not connected
  S1 = Pushbutton [package="[THT]"]

nets:
  N1: Part1.D8, HC-SR04_Sensor_1.TRIG
  N2: Part1.D9_PWM, HC-SR04_Sensor_1.ECHO
  N3: Part1.D4, S1.Pin_1, S1.Pin_2, S1.Pin_3, S1.Pin_4
  5V: Part1.5V, HC-SR04_Sensor_1.VCC
  GND: Part1.GND, HC-SR04_Sensor_1.GND

notes:
  I2C LCD =
  GND(LCD) - GND(UNO)
  5V(LCD) - 5V(UNO)
  SDA(LCD) - A4(UNO)
  SCL(LCD) - A5(UNO)
